// Logisim project ProcessorNamık.circ as structural Verilog: 15 circuits, main circuit SR Latch
module SR_Latch (
  input  S__set,
  input  R__reset,
  output Q
);

  wire nor_1_out;

  nor nor_1 (nor_1_out, S__set, Q);
  nor nor_2 (Q, nor_1_out, R__reset);
endmodule

module D_Latch (
  input  D,
  input  clk,
  output Q
);

  wire and_1_out, and_2_out, not_1_out;

  not not_1 (not_1_out, D);
  and and_1 (and_1_out, D, clk);
  and and_2 (and_2_out, clk, not_1_out);
  SR_Latch SR_Latch (.S__set(and_1_out), .R__reset(and_2_out), .Q(Q));
endmodule

module D_Flip_Flop (
  input  D,
  input  clk,
  output Q
);

  wire D_Latch__master_q, not_1_out;

  not not_1 (not_1_out, clk);
  D_Latch D_Latch__master (.D(D), .clk(not_1_out), .Q(D_Latch__master_q));
  D_Latch D_Latch__servant (.D(D_Latch__master_q), .clk(clk), .Q(Q));
endmodule

// 2 R
module _2_bit_Register (
  input  I1,
  input  I0,
  input  clk,
  output Q1,
  output Q0
);

  D_Flip_Flop Flip_Flop (.D(I1), .clk(clk), .Q(Q1));
  D_Flip_Flop Flip_Flop_2 (.D(I0), .clk(clk), .Q(Q0));
endmodule

// 4 R
module _4_bit_Register (
  input  I3,
  input  I2,
  input  I1,
  input  I0,
  input  clk,
  output Q3,
  output Q2,
  output Q1,
  output Q0
);

  _2_bit_Register u_2_bit_register_1 (.clk(clk), .I1(I3), .I0(I2), .Q1(Q3), .Q0(Q2));
  _2_bit_Register u_2_bit_register_2 (.clk(clk), .I1(I1), .I0(I0), .Q1(Q1), .Q0(Q0));
endmodule

// 8 R
module _8_bit_Register (
  input  I7,
  input  I6,
  input  I5,
  input  I4,
  input  I3,
  input  I2,
  input  I1,
  input  I0,
  input  clk,
  output Q7,
  output Q6,
  output Q5,
  output Q4,
  output Q3,
  output Q2,
  output Q1,
  output Q0
);

  _4_bit_Register u_4_bit_register_1 (
    .clk(clk), .I3(I7), .I2(I6), .I1(I5), .I0(I4), .Q3(Q7), .Q2(Q6), .Q1(Q5), .Q0(Q4));
  _4_bit_Register u_4_bit_register_2 (
    .clk(clk), .I3(I3), .I2(I2), .I1(I1), .I0(I0), .Q3(Q3), .Q2(Q2), .Q1(Q1), .Q0(Q0));
endmodule

module _12_bit_Register (
  input  I11,
  input  I10,
  input  I9,
  input  I8,
  input  I7,
  input  I6,
  input  I5,
  input  I4,
  input  I3,
  input  I2,
  input  I1,
  input  I0,
  input  clk,
  output Q11,
  output Q10,
  output Q9,
  output Q8,
  output Q7,
  output Q6,
  output Q5,
  output Q4,
  output Q3,
  output Q2,
  output Q1,
  output Q0
);

  _8_bit_Register u_8_bit_register_1 (
    .clk(clk), .I7(I11), .I6(I10), .I5(I9), .I4(I8), .I3(I7), .I2(I6), .I1(I5), .I0(I4), .Q7(Q11), .Q6(Q10),
    .Q5(Q9), .Q4(Q8), .Q3(Q7), .Q2(Q6), .Q1(Q5), .Q0(Q4));
  _4_bit_Register u_4_bit_register_1 (
    .clk(clk), .I3(I3), .I2(I2), .I1(I1), .I0(I0), .Q3(Q3), .Q2(Q2), .Q1(Q1), .Q0(Q0));
endmodule

module _16_bit_Register (
  input  I15,
  input  I14,
  input  I13,
  input  I12,
  input  I11,
  input  I10,
  input  I9,
  input  I8,
  input  I7,
  input  I6,
  input  I5,
  input  I4,
  input  I3,
  input  I2,
  input  I1,
  input  I0,
  input  clk,
  output Q15,
  output Q14,
  output Q13,
  output Q12,
  output Q11,
  output Q10,
  output Q9,
  output Q8,
  output Q7,
  output Q6,
  output Q5,
  output Q4,
  output Q3,
  output Q2,
  output Q1,
  output Q0
);

  _8_bit_Register u_8_bit_register_1 (
    .clk(clk), .I7(I15), .I6(I14), .I5(I13), .I4(I12), .I3(I11), .I2(I10), .I1(I9), .I0(I8), .Q7(Q15),
    .Q6(Q14), .Q5(Q13), .Q4(Q12), .Q3(Q11), .Q2(Q10), .Q1(Q9), .Q0(Q8));
  _8_bit_Register u_8_bit_register_2 (
    .clk(clk), .I7(I7), .I6(I6), .I5(I5), .I4(I4), .I3(I3), .I2(I2), .I1(I1), .I0(I0), .Q7(Q7), .Q6(Q6),
    .Q5(Q5), .Q4(Q4), .Q3(Q3), .Q2(Q2), .Q1(Q1), .Q0(Q0));
endmodule

// Reg-File
module Register_File (
  input  [3:0] register,
  input  [15:0] value,
  input  write,
  input  clk,
  output [15:0] \output 
);

  wire decoder_1_out0, decoder_1_out1, decoder_1_out2, decoder_1_out3, decoder_1_out4, decoder_1_out5,
       decoder_1_out6, decoder_1_out7, decoder_1_out8, decoder_1_out9, decoder_1_out10, decoder_1_out11,
       decoder_1_out12, decoder_1_out13, decoder_1_out14, decoder_1_out15;
  wire [15:0] register_1_q, register_2_q, register_3_q, register_4_q, register_5_q, register_6_q,
       register_7_q, register_8_q, register_9_q, register_10_q, register_11_q, register_12_q, register_13_q,
       register_14_q, register_15_q, register_16_q;

  Decoder #(.select(4), .disabled(0)) decoder_1 (
    .out0(decoder_1_out0), .out1(decoder_1_out1), .out2(decoder_1_out2), .out3(decoder_1_out3),
    .out4(decoder_1_out4), .out5(decoder_1_out5), .out6(decoder_1_out6), .out7(decoder_1_out7),
    .out8(decoder_1_out8), .out9(decoder_1_out9), .out10(decoder_1_out10), .out11(decoder_1_out11),
    .out12(decoder_1_out12), .out13(decoder_1_out13), .out14(decoder_1_out14), .out15(decoder_1_out15),
    .sel(register), .en(write));
  Register #(.width(16)) register_1 (.D(value), .en(decoder_1_out0), .Q(register_1_q), .clk(clk));  // open: clr
  Register #(.width(16)) register_2 (.D(value), .en(decoder_1_out1), .Q(register_2_q), .clk(clk));  // open: clr
  Register #(.width(16)) register_3 (.D(value), .en(decoder_1_out2), .Q(register_3_q), .clk(clk));  // open: clr
  Register #(.width(16)) register_4 (.D(value), .en(decoder_1_out3), .Q(register_4_q), .clk(clk));  // open: clr
  Register #(.width(16)) register_5 (.D(value), .en(decoder_1_out4), .Q(register_5_q), .clk(clk));  // open: clr
  Register #(.width(16)) register_6 (.D(value), .en(decoder_1_out5), .Q(register_6_q), .clk(clk));  // open: clr
  Register #(.width(16)) register_7 (.D(value), .en(decoder_1_out6), .Q(register_7_q), .clk(clk));  // open: clr
  Register #(.width(16)) register_8 (.D(value), .en(decoder_1_out7), .Q(register_8_q), .clk(clk));  // open: clr
  Register #(.width(16)) register_9 (.D(value), .en(decoder_1_out8), .Q(register_9_q), .clk(clk));  // open: clr
  Register #(.width(16)) register_10 (.D(value), .en(decoder_1_out9), .Q(register_10_q), .clk(clk));  // open: clr
  Register #(.width(16)) register_11 (.D(value), .en(decoder_1_out10), .Q(register_11_q), .clk(clk));  // open: clr
  Register #(.width(16)) register_12 (.D(value), .en(decoder_1_out11), .Q(register_12_q), .clk(clk));  // open: clr
  Register #(.width(16)) register_13 (.D(value), .en(decoder_1_out12), .Q(register_13_q), .clk(clk));  // open: clr
  Register #(.width(16)) register_14 (.D(value), .en(decoder_1_out13), .Q(register_14_q), .clk(clk));  // open: clr
  Register #(.width(16)) register_15 (.D(value), .en(decoder_1_out14), .Q(register_15_q), .clk(clk));  // open: clr
  Register #(.width(16)) register_16 (.D(value), .en(decoder_1_out15), .Q(register_16_q), .clk(clk));  // open: clr
  Multiplexer #(.select(4), .width(16), .disabled(0)) multiplexer_1 (
    .in0(register_1_q), .in1(register_2_q), .in2(register_3_q), .in3(register_4_q), .in4(register_5_q),
    .in5(register_6_q), .in6(register_7_q), .in7(register_8_q), .in8(register_9_q), .in9(register_10_q),
    .in10(register_11_q), .in11(register_12_q), .in12(register_13_q), .in13(register_14_q),
    .in14(register_15_q), .in15(register_16_q), .out(\output ), .sel(register));  // open: en
endmodule

// HA
module Half_Adder (
  input  a,
  input  b,
  output carry_out,
  output sum
);

  and and_1 (carry_out, b, a);
  xor xor_1 (sum, b, a);
endmodule

// FA
module Full_Adder (
  input  a,
  input  b,
  input  carry_in,
  output carry_out,
  output sum
);

  wire and_1_out, and_2_out, and_3_out;

  and and_1 (and_1_out, a, b);
  and and_2 (and_2_out, a, carry_in);
  and and_3 (and_3_out, b, carry_in);
  ExactlyOne xor_1 (.out(sum), .in0(carry_in), .in1(b), .in2(a));
  or or_1 (carry_out, and_1_out, and_2_out, and_3_out);
endmodule

// 4 A
module _4_bit_Adder (
  input  [3:0] a,
  input  [3:0] b,
  input  carry_in,
  output carry_out,
  output [3:0] \output 
);

  wire full_adder_1_carry_out, full_adder_2_carry_out, full_adder_3_carry_out;

  Full_Adder full_adder_1 (
    .a(a[0]), .b(b[0]), .carry_in(carry_in), .carry_out(full_adder_1_carry_out), .sum(\output [0]));
  Full_Adder full_adder_2 (
    .a(a[1]), .b(b[1]), .carry_in(full_adder_1_carry_out), .carry_out(full_adder_2_carry_out),
    .sum(\output [1]));
  Full_Adder full_adder_3 (
    .a(a[2]), .b(b[2]), .carry_in(full_adder_2_carry_out), .carry_out(full_adder_3_carry_out),
    .sum(\output [2]));
  Full_Adder full_adder_4 (
    .a(a[3]), .b(b[3]), .carry_in(full_adder_3_carry_out), .carry_out(carry_out), .sum(\output [3]));
endmodule

// 8 A
module _8_bit_Adder (
  input  [7:0] a,
  input  [7:0] b,
  input  carry_in,
  output carry_out,
  output [7:0] out_5
);

  wire n4_bit_adder_1_carry_out;

  _4_bit_Adder u_4_bit_adder_1 (
    .a(a[3:0]), .b(b[3:0]), .carry_in(carry_in), .carry_out(n4_bit_adder_1_carry_out), .\output (out_5[3:0]));
  _4_bit_Adder u_4_bit_adder_2 (
    .a(a[7:4]), .b(b[7:4]), .carry_in(n4_bit_adder_1_carry_out), .carry_out(carry_out), .\output (out_5[7:4]));
endmodule

// 16 A
module _16_bit_Adder (
  input  [15:0] a,
  input  [15:0] b,
  input  carry_in,
  output carry_out,
  output [15:0] \output 
);

  wire n8_bit_adder_1_carry_out;

  _8_bit_Adder u_8_bit_adder_1 (
    .a(a[7:0]), .b(b[7:0]), .carry_in(carry_in), .carry_out(n8_bit_adder_1_carry_out), .out_5(\output [7:0]));
  _8_bit_Adder u_8_bit_adder_2 (
    .a(a[15:8]), .b(b[15:8]), .carry_in(n8_bit_adder_1_carry_out), .carry_out(carry_out),
    .out_5(\output [15:8]));
endmodule

module Incrementer (
  input  [11:0] \input ,
  input  carry_in,
  output carry_out,
  output [11:0] \output 
);

  wire n4_bit_adder_1_carry_out;

  _4_bit_Adder u_4_bit_adder_1 (
    .a(\input [3:0]), .b(4'b0001), .carry_in(carry_in), .carry_out(n4_bit_adder_1_carry_out),
    .\output (\output [3:0]));
  _8_bit_Adder u_8_bit_adder_1 (
    .a(\input [11:4]), .b({8{1'b0}}), .carry_in(n4_bit_adder_1_carry_out), .carry_out(carry_out),
    .out_5(\output [11:4]));
endmodule
